// Logisim project ALU.circ as structural Verilog: 2 circuits, main circuit main
module main (
  input  [2:0] ALUOp,
  input  [15:0] A,
  input  [15:0] B,
  input  [15:0] in_4,
  output [15:0] Result,
  output [15:0] Result2,
  output GT,
  output Zero,
  output LT
);

  wire [15:0] ADD, AND, DIV, DIV2, LEFT, MUL, MUL2, NOR, RIGHT, SUB;

  assign AND = A & B;  // AND_Gate and_1, 16 bits wide
  assign NOR = ~(A | B);  // NOR_Gate nor_1, 16 bits wide
  Comparator #(.width(16)) comparator_1 (.a(A), .b(in_4), .gt(GT), .eq(Zero), .lt(LT));
  Adder #(.width(16)) adder_1 (.a(A), .b(B), .out(ADD));  // open: cin, cout
  Subtractor #(.width(16)) subtractor_1 (.a(A), .b(B), .out(SUB));  // open: bin, bout
  Multiplier #(.width(16)) multiplier_1 (.a(A), .b(B), .out(MUL), .cout(MUL2));  // open: cin
  Divider #(.width(16)) divider_1 (.a(A), .b(B), .out(DIV), .rem(DIV2));  // open: upper
  Shifter #(.width(16)) shifter_1 (.in(A), .\dist (B[3:0]), .out(LEFT));
  Shifter #(.width(16), .shift("lr")) shifter_2 (.in(A), .\dist (B[3:0]), .out(RIGHT));
  Multiplexer #(.select(3), .width(16)) multiplexer_1 (
    .in0(in_4), .in1(in_4), .in2(in_4), .in3(in_4), .in4(MUL2), .in5(DIV2), .in6(in_4), .in7(in_4),
    .out(Result2), .sel(ALUOp));  // open: en
  Multiplexer #(.select(3), .width(16)) multiplexer_2 (
    .in0(AND), .in1(NOR), .in2(ADD), .in3(SUB), .in4(MUL), .in5(DIV), .in6(LEFT), .in7(RIGHT), .out(Result),
    .sel(ALUOp));  // open: en

  // Other names for the same wires on the sheet: c[15:0] = in_4

  // Notes on the sheet:
  //   Trinity Zenet Yue Key (tzk1)
  //   Inputs
  //   Design your ALU in this file
  //   A - First ALU input
  //   B - Second ALU input
  //   Result - ALU main result
  //   Result2 - Output for MSB of mul/div operations
  //   GT/Zero/LT - Comparison of input A with zero
  //   ALUOp - The control signal defining the behaviour of the ALU
  //    Don't modify any of the inputs/outputs in this file!
  //   Outputs
endmodule

module test (
);

  main main_1 ();  // open: ALUOp, A, B, Result, GT, Zero, LT, Result2, in_4

  // Notes on the sheet:
  //   Test your circuit!
endmodule
