// Logisim project RegFile.circ as structural Verilog: 2 circuits, main circuit main
module main (
  input  [15:0] WriteData0,
  input  [15:0] WriteData1,
  input  [2:0] WriteSelect0,
  input  [2:0] ReadSelect0,
  input  [2:0] ReadSelect1,
  input  WE0,
  input  WE1,
  input  Clock,
  output [15:0] Reg0,
  output [15:0] Reg1,
  output [15:0] Reg2,
  output [15:0] Reg3,
  output [15:0] Reg4,
  output [15:0] Reg5,
  output [15:0] Reg6,
  output [15:0] Reg7,
  output [15:0] ReadData0,
  output [15:0] ReadData1
);

  wire A0, A1, B0, B1, C0, C1, D0, D1, E0, E1, F0, F1, G0, G1, H0, H1, xor_2_out, xor_4_out, xor_6_out,
       xor_8_out, xor_10_out, xor_12_out, xor_14_out, xor_16_out;
  wire [2:0] adder_1_out, adder_2_out;
  wire [15:0] D00, D01, D02, D03, D04, D05, D06, D07, D10, D11, D12, D13, D14, D15, D16, D17, undriven,
       undriven_2, undriven_3, undriven_4, undriven_5, undriven_6, undriven_7, undriven_8, undriven_9,
       undriven_10, xor_1_out, xor_3_out, xor_5_out, xor_7_out, xor_9_out, xor_11_out, xor_13_out, xor_15_out;

  Demultiplexer #(.select(3)) demultiplexer_1 (
    .out0(A0), .out1(B0), .out2(H0), .out3(C0), .out4(D0), .out5(E0), .out6(F0), .out7(G0), .in(WE0),
    .sel(WriteSelect0));  // open: en
  Demultiplexer #(.select(3)) demultiplexer_2 (
    .out0(A1), .out1(B1), .out2(H1), .out3(C1), .out4(D1), .out5(E1), .out6(F1), .out7(G1), .in(WE1),
    .sel(adder_1_out));  // open: en
  Adder #(.width(3)) adder_1 (.a(WriteSelect0), .b(3'b001), .out(adder_1_out));  // open: cin, cout
  Demultiplexer #(.select(3), .width(16)) demultiplexer_3 (
    .out0(D00), .out1(D01), .out2(D02), .out3(D03), .out4(D04), .out5(D05), .out6(D06), .out7(D07),
    .in(WriteData0), .sel(WriteSelect0));  // open: en
  Demultiplexer #(.select(3), .width(16)) demultiplexer_4 (
    .out0(D10), .out1(D11), .out2(D12), .out3(D13), .out4(D14), .out5(D15), .out6(D16), .out7(D17),
    .in(WriteData1), .sel(adder_2_out));  // open: en
  Adder #(.width(3)) adder_2 (.a(WriteSelect0), .b(3'b001), .out(adder_2_out));  // open: cin, cout
  ExactlyOne xor_1[15:0] (.out(xor_1_out), .in1(D00), .in3(D10), .in4(undriven));
  ExactlyOne xor_2 (.out(xor_2_out), .in0(undriven[0]), .in1(A0), .in3(A1));
  ExactlyOne xor_3[15:0] (.out(xor_3_out), .in1(D01), .in3(D11), .in4(undriven_2));
  ExactlyOne xor_4 (.out(xor_4_out), .in0(undriven_2[0]), .in1(B0), .in3(B1));
  ExactlyOne xor_5[15:0] (.out(xor_5_out), .in1(D02), .in3(D12), .in4(undriven_3));
  ExactlyOne xor_6 (.out(xor_6_out), .in0(undriven_3[0]), .in1(H0), .in3(H1));
  ExactlyOne xor_7[15:0] (.out(xor_7_out), .in1(D03), .in3(D13), .in4(undriven_4));
  ExactlyOne xor_8 (.out(xor_8_out), .in0(undriven_4[0]), .in1(C0), .in3(C1));
  ExactlyOne xor_9[15:0] (.out(xor_9_out), .in1(D04), .in3(D14), .in4(undriven_5));
  ExactlyOne xor_10 (.out(xor_10_out), .in0(undriven_5[0]), .in1(D0), .in3(D1));
  ExactlyOne xor_11[15:0] (.out(xor_11_out), .in1(D05), .in3(D15), .in4(undriven_6));
  ExactlyOne xor_12 (.out(xor_12_out), .in0(undriven_6[0]), .in1(E0), .in3(E1), .in4(undriven_7[0]));
  ExactlyOne xor_13[15:0] (.out(xor_13_out), .in0(undriven_7), .in1(D06), .in3(D16), .in4(undriven_8));
  ExactlyOne xor_14 (.out(xor_14_out), .in0(undriven_8[0]), .in1(F0), .in3(F1), .in4(undriven_9[0]));
  ExactlyOne xor_15[15:0] (.out(xor_15_out), .in0(undriven_9), .in1(D07), .in3(D17), .in4(undriven_10));
  ExactlyOne xor_16 (.out(xor_16_out), .in0(undriven_10[0]), .in1(G0), .in3(G1));
  Register #(.width(16)) u_reg0 (.D(xor_1_out), .en(xor_2_out), .Q(Reg0), .clk(Clock));  // open: clr
  Register #(.width(16)) u_reg1 (.D(xor_3_out), .en(xor_4_out), .Q(Reg1), .clk(Clock));  // open: clr
  Register #(.width(16)) u_reg2 (.D(xor_5_out), .en(xor_6_out), .Q(Reg2), .clk(Clock));  // open: clr
  Register #(.width(16)) u_reg3 (.D(xor_7_out), .en(xor_8_out), .Q(Reg3), .clk(Clock));  // open: clr
  Register #(.width(16)) u_reg4 (.D(xor_9_out), .en(xor_10_out), .Q(Reg4), .clk(Clock));  // open: clr
  Register #(.width(16)) u_reg5 (.D(xor_11_out), .en(xor_12_out), .Q(Reg5), .clk(Clock));  // open: clr
  Register #(.width(16)) u_reg6 (.D(xor_13_out), .en(xor_14_out), .Q(Reg6), .clk(Clock));  // open: clr
  Register #(.width(16)) u_reg7 (.D(xor_15_out), .en(xor_16_out), .Q(Reg7), .clk(Clock));  // open: clr
  Multiplexer #(.select(3), .width(16)) multiplexer_1 (
    .in0(Reg0), .in1(Reg1), .in2(Reg2), .in3(Reg3), .in4(Reg4), .in5(Reg5), .in6(Reg6), .in7(Reg7),
    .out(ReadData0), .sel(ReadSelect0));  // open: en
  Multiplexer #(.select(3), .width(16)) multiplexer_2 (
    .in0(Reg0), .in1(Reg1), .in2(Reg2), .in3(Reg3), .in4(Reg4), .in5(Reg5), .in6(Reg6), .in7(Reg7),
    .out(ReadData1), .sel(ReadSelect1));  // open: en
  // Pins of 1 and 16 bits meet at undriven_4
  // Pins of 1 and 16 bits meet at undriven
  // Pins of 1 and 16 bits meet at undriven_5
  // Pins of 1 and 16 bits meet at undriven_3
  // Pins of 1 and 16 bits meet at undriven_2
  // Pins of 1 and 16 bits meet at undriven_7
  // Pins of 1 and 16 bits meet at undriven_8
  // Pins of 1 and 16 bits meet at undriven_6
  // Pins of 1 and 16 bits meet at undriven_9
  // Pins of 1 and 16 bits meet at undriven_10

  // Other names for the same wires on the sheet: WriteEnable0 = WE0; WriteEnable1 = WE1

  // Notes on the sheet:
  //   Inputs
  //   WriteSelect0 - Register to write to
  //   WE0 - Enable writing to 1 register
  //   These can be used for debug and testing
  //   Add the registers to this file
  //   ReadSelect0 - First register to read data from
  //   ReadSelect1 - Second register to read data from
  //   WE1 - Enable writing to 2nd register (mul/div)
  //   ReadData0 - Data being read from first register
  //   ReadData1 - Data being read from second register
  //   WriteData0 - The data to be written to register by most instructions
  //   WriteData1 - The data to be written to second register by mul/div
  //    Don't modify any of the inputs/outputs in this file!
  //   and design the logic to control them
  //   Outputs
endmodule

module test (
  input  [15:0] Write_data_A,
  input  Write_Enable_Port_A,
  input  [2:0] in_3,
  input  [15:0] Write_data_B,
  input  Write_Enable_Port_B,
  input  [2:0] Select_Read_A,
  input  [2:0] Select_Read_B
);

  wire Clock_out;
  wire [15:0] main_1_readdata0, main_1_readdata1, main_1_reg0, main_1_reg1, main_1_reg2, main_1_reg3,
       main_1_reg4, main_1_reg5, main_1_reg6, main_1_reg7;

  // Probe on main_1_reg0
  // Probe on main_1_reg1
  // Probe on main_1_reg2
  // Probe on main_1_reg3
  Button Clock (.out(Clock_out));
  // Probe on main_1_reg5
  // Probe on main_1_reg4
  // Probe on main_1_reg6
  // Probe on main_1_reg7
  main main_1 (
    .WriteData0(Write_data_A), .WriteData1(Write_data_B), .ReadData0(main_1_readdata0),
    .ReadData1(main_1_readdata1), .WriteSelect0(in_3), .ReadSelect0(Select_Read_A),
    .ReadSelect1(Select_Read_B), .Reg0(main_1_reg0), .Reg1(main_1_reg1), .Reg2(main_1_reg2),
    .Reg3(main_1_reg3), .Reg4(main_1_reg4), .Reg5(main_1_reg5), .Reg6(main_1_reg6), .Reg7(main_1_reg7),
    .WE0(Write_Enable_Port_A), .WE1(Write_Enable_Port_B), .Clock(Clock_out));
  // Probe on main_1_readdata0
  // Probe on main_1_readdata1

  // Notes on the sheet:
  //   Test your circuit!
endmodule
