// Logisim project umips.circ as structural Verilog: 4 circuits, main circuit main
module main (
  output [15:0] Reg0,
  output [15:0] Reg1,
  output [15:0] Reg2,
  output [15:0] Reg3,
  output [15:0] Reg4,
  output [15:0] Reg5,
  output [15:0] Reg6,
  output [15:0] Reg7,
  output [3:0] Output3,
  output [3:0] Output2,
  output [3:0] Output1,
  output [3:0] Output0,
  output halt
);

  wire Clock, decoder_1_load_word, greater_than, jump, jump_imm, less_than, load_word, not_1_out, put,
       store_word, subop, WEA, WEB, zero;
  wire [1:0] sign_operation, WriteData;
  wire [2:0] ALUOp, rs, rt;
  wire [3:0] opcode;
  wire [7:0] adder_1_out, adder_2_out, immediate, multiplexer_1_out, multiplexer_3_out, PC, Reg_A;
  wire [15:0] bit_extender_1_out, bit_extender_2_out, bit_extender_3_out, bit_extender_4_out, instruction,
       RAM, Reg_B, RegB, Result, Result2, WDataA;
  wire [15:8] RegA;

  Clock clock_1 (.out(Clock));
  Hex_Digit_Display hex_digit_display_1 (.value(Output3));  // open: dp
  Hex_Digit_Display hex_digit_display_2 (.value(Output2));  // open: dp
  hex hex_1 (
    .rs({RegA, Reg_A}), .put(put), .out_4(Output3), .out_5(Output2), .out_6(Output1), .out_7(Output0),
    .clock(Clock));
  Hex_Digit_Display hex_digit_display_3 (.value(Output0));  // open: dp
  Hex_Digit_Display hex_digit_display_4 (.value(Output1));  // open: dp
  assign bit_extender_1_out = {{8{1'b0}}, immediate};  // Bit_Extender bit_extender_1
  assign bit_extender_2_out = {{8{immediate[7]}}, immediate};  // Bit_Extender bit_extender_2
  Multiplexer #(.width(8)) multiplexer_1 (
    .in0(Reg_A), .in1(immediate), .out(multiplexer_1_out), .sel(jump_imm));  // open: en
  decoder decoder_1 (
    .greater_than(greater_than), .less_than(less_than), .equal_to(zero), .subop(subop), .opcode(opcode),
    .store_word(store_word), .load_word(decoder_1_load_word), .put(put), .halt(halt),
    .sign_operation(sign_operation), .WriteData(WriteData), .jump(jump), .jump_imm(jump_imm), .ALUOp(ALUOp),
    .WEA(WEA), .WEB(WEB));
  Multiplexer #(.select(2), .width(16)) multiplexer_2 (
    .in0(RegB), .in1(bit_extender_1_out), .in2(bit_extender_2_out), .out(Reg_B), .sel(sign_operation));  // open: in3, en
  Adder adder_1 (.a(PC), .b(8'h1), .out(adder_1_out));  // open: cin, cout
  Multiplexer #(.width(8)) multiplexer_3 (
    .in0(adder_1_out), .in1(multiplexer_1_out), .out(multiplexer_3_out), .sel(jump));  // open: en
  ALU_main main_1 (
    .ALUOp(ALUOp), .A({RegA, Reg_A}), .B(Reg_B), .Result(Result), .GT(greater_than), .Zero(zero),
    .LT(less_than), .Result2(Result2));  // open: in_4
  Register u_PC (.D(multiplexer_3_out), .en(not_1_out), .Q(PC), .clk(Clock));  // open: clr
  not not_1 (not_1_out, halt);
  ROM #(.dataWidth(16)) rom_1 (.addr(PC), .data(instruction), .sel(1'b1));
  LED led_1 (.in(halt));
  fields fields_1 (.fields(instruction), .subop(subop), .immediate(immediate), .rs(rs), .opcode(opcode), .rt(rt));
  Adder adder_2 (.a(PC), .b(8'h1), .out(adder_2_out));  // open: cin, cout
  assign bit_extender_3_out = {{8{1'b0}}, immediate};  // Bit_Extender bit_extender_3
  assign bit_extender_4_out = {{8{1'b0}}, adder_2_out};  // Bit_Extender bit_extender_4
  RAM #(.dataWidth(16), .bus("separate")) ram_1 (
    .addr(RegB[7:0]), .din({RegA, Reg_A}), .data(RAM), .str(store_word), .sel(1'b1), .clk(Clock),
    .ld(load_word));  // open: clr
  Multiplexer #(.select(2), .width(16)) multiplexer_4 (
    .in0(bit_extender_4_out), .in1(bit_extender_3_out), .in2(RAM), .in3(Result), .out(WDataA), .sel(WriteData));  // open: en
  RegFile_main main_2 (
    .WriteData0(WDataA), .WriteData1(Result2), .ReadData0({RegA, Reg_A}), .ReadData1(RegB),
    .WriteSelect0(rs), .ReadSelect0(rs), .ReadSelect1(rt), .Reg0(Reg0), .Reg1(Reg1), .Reg2(Reg2),
    .Reg3(Reg3), .Reg4(Reg4), .Reg5(Reg5), .Reg6(Reg6), .Reg7(Reg7), .WE0(WEA), .WE1(WEB), .Clock(Clock));

  // Other names for the same wires on the sheet: RegA[7:0] = Reg_A

  // Notes on the sheet:
  //    Don't modify these, they are used for debug and testing
  //   Design your CPU in this file
  //   You must connect Reg0..7 to the top ports of the register file.
  //   Include everything here (ALU, RegFile, Control, PC, RAM, ROM, LEDs, Displays, ...)
  //   Connect Output3..0 to your LED display.
  //   Output3 is the most significant
  //   Connect halt to your halt LED
endmodule

module fields (
  input  [15:0] fields,
  output [2:0] rt,
  output subop,
  output [7:0] immediate,
  output [2:0] rs,
  output [3:0] opcode
);


  assign immediate = fields[8:1];
  assign opcode = fields[15:12];
  assign rs = fields[11:9];
  assign rt = fields[8:6];
  assign subop = fields[0];
endmodule

module hex (
  input  [15:0] rs,
  input  put,
  input  clock,
  output [3:0] out_4,
  output [3:0] out_5,
  output [3:0] out_6,
  output [3:0] out_7
);

  Register #(.width(16)) register_1 (.D(rs), .en(put), .Q({out_4, out_5, out_6, out_7}), .clk(clock));  // open: clr
endmodule

module decoder (
  input  greater_than,
  input  less_than,
  input  equal_to,
  input  subop,
  input  [3:0] opcode,
  output store_word,
  output load_word,
  output put,
  output halt,
  output [1:0] sign_operation,
  output [1:0] WriteData,
  output jump,
  output jump_imm,
  output [2:0] ALUOp,
  output WEA,
  output WEB
);

  wire add, addi, addui, \and , and_1_out, and_2_out, and_3_out, and_4_out, bn, bp, branch, bx, bz,
       decoder_1_out8, decoder_1_out9, decoder_1_out16, decoder_1_out17, decoder_1_out18, decoder_1_out19,
       decoder_1_out20, decoder_1_out21, decoder_1_out22, decoder_1_out23, decoder_1_out24, decoder_1_out25,
       decoder_1_out26, decoder_1_out27, decoder_1_out28, decoder_1_out29, decoder_1_out30, decoder_1_out31,
       div, jal, jr, jump_imm_t, li, mul, \nor , or_1_out, or_2_out, or_7_out, sllv, srlv, sub, undriven,
       undriven_2;

  Priority_Encoder #(.select(2)) priority_encoder_1 (
    .in0(1'b1), .in1(addui), .in2(addi), .out(sign_operation));  // open: in3, gs, en_out, en_in
  or or_1 (or_1_out, add, addi, addui);
  or or_2 (or_2_out, add, addi, addui, sub, \and , mul, div, \nor , srlv, sllv);
  or or_3 (jump, jr, jal, jump_imm_t, branch);
  or or_4 (jump_imm, jal, jump_imm_t, branch);
  Priority_Encoder #(.select(2)) priority_encoder_2 (
    .in0(jal), .in1(li), .in2(load_word), .in3(or_2_out), .out(WriteData));  // open: gs, en_out, en_in
  or or_5 (WEA, jal, li, mul, load_word, or_1_out, srlv, sllv, \and , sub, \nor , div);
  or or_6 (WEB, mul, div);
  and and_1 (and_1_out, greater_than, greater_than, bp, undriven);
  and and_2 (and_2_out, undriven, less_than, bn);
  and and_3 (and_3_out, bx, undriven_2);  // AND_Gate
  and and_4 (and_4_out, undriven_2, equal_to, bz);
  or or_7 (or_7_out, add, addui, addi);
  Decoder #(.select(5)) decoder_1 (
    .out0(add), .out1(sub), .out2(\nor ), .out3(\and ), .out4(mul), .out5(div), .out6(addui), .out7(addi),
    .out8(decoder_1_out8), .out9(decoder_1_out9), .out10(li), .out12(srlv), .out13(sllv), .out14(store_word),
    .out15(load_word), .out16(decoder_1_out16), .out17(decoder_1_out17), .out18(decoder_1_out18),
    .out19(decoder_1_out19), .out20(decoder_1_out20), .out21(decoder_1_out21), .out22(decoder_1_out22),
    .out23(decoder_1_out23), .out24(decoder_1_out24), .out25(decoder_1_out25), .out26(decoder_1_out26),
    .out27(decoder_1_out27), .out28(decoder_1_out28), .out29(decoder_1_out29), .out30(decoder_1_out30),
    .out31(decoder_1_out31), .sel({opcode, subop}));  // open: out11, en
  or or_8 (branch, and_2_out, and_2_out, and_3_out, and_3_out);
  Priority_Encoder priority_encoder_3 (
    .in0(\and ), .in1(\nor ), .in2(or_7_out), .in3(sub), .in4(mul), .in5(div), .in6(sllv), .in7(srlv),
    .out(ALUOp));  // open: en_in, gs, en_out
  or or_9 (bp, decoder_1_out8, decoder_1_out9);
  // OR_Gate or_10: pin names not known; wires that end beside it: decoder_1_out16, decoder_1_out17, put
  // OR_Gate or_11: pin names not known; wires that end beside it: decoder_1_out18, decoder_1_out19, halt
  // OR_Gate or_12: pin names not known; wires that end beside it: decoder_1_out20, decoder_1_out21, jal
  // OR_Gate or_13: pin names not known; wires that end beside it: decoder_1_out22, decoder_1_out23, jump_imm_t
  // OR_Gate or_14: pin names not known; wires that end beside it: decoder_1_out24, decoder_1_out25, bn
  // OR_Gate or_15: pin names not known; wires that end beside it: decoder_1_out26, decoder_1_out27, bx
  // OR_Gate or_16: pin names not known; wires that end beside it: decoder_1_out28, decoder_1_out29, jr
  or or_17 (bz, decoder_1_out30, decoder_1_out31);
endmodule
